# Fritzing sketch Wiring (saved by Fritzing 0.9.3b)

parts:
  DFPlayer_Mini1 = DFPlayer MINI [package="DIP (Dual Inline) [THT]"]
  SPKR1 = Loudspeaker
  R1 = Resistor [tolerance=±5% resistance=1k package=THT]
  Composant2 = Real Time Clock Module - DS1307 RTC Breakout Board
  Composant3 = Arduino Uno (Rev3)
  X1 = USB Connectors [package=usb-a-s-nosilk-female]
  JP3 = Header 4 [package=screwterminal-3.5mm-4_lock]
  JP2 = Header 4 [package=screwterminal-3.5mm-4_lock]
  U1 = SWITCH_SPDT [package=kps-1290]
  U2 = RELAY [package=relay-t9a]
  U3 = SWITCH_SPDT [package=kps-1290]
  R2 = Resistor [tolerance=±5% resistance=220 package=THT]
  Q1 = NPN-Transistor [package="TO92 [THT]"]
  D1 = Rectifier Diode [part_number=1N4001 package="300 mil [THT]"]
  R3 = Resistor [tolerance=±5% resistance=220 package=THT]
  JP5 = Header 4 [package=screwterminal-3.5mm-4_lock]
  S1 = Pushbutton [package="[THT]"]

nets:
  5V: DFPlayer_Mini1.VCC, Composant2.5V, Composant3.5V, X1.D+, JP2.1, U2.COIL1, R2.Pin_1, JP5.2, S1.Pin_1, S1.Pin_2
  N1: DFPlayer_Mini1.RX, R1.Pin_1
  N2: DFPlayer_Mini1.TX, Composant3.D6_PWM
  N3: DFPlayer_Mini1.SPK1, U1.S
  GND: DFPlayer_Mini1.GND, Composant2.GND, Composant3.GND, X1.D-, JP2.2, Q1.E, JP5.1
  N4: DFPlayer_Mini1.SPK2, SPKR1.pin1
  N5: SPKR1.pin2, U2.MAIN
  N6: R1.Pin_0, Composant3.D7
  N7: Composant2.SCL, Composant3.A5/SCL
  N8: Composant2.SDA, Composant3.A4/SDA
  N9: Composant3.D8, JP2.4
  N10: Composant3.D9_PWM, JP3.1
  N11: Composant3.D10_PWM/SS, JP2.3
  N12: Composant3.D11_PWM/MOSI, JP3.2
  N13: Composant3.D12/MISO, S1.Pin_3, S1.Pin_4
  N14: Composant3.D13/SCK, JP3.3
  N15: Composant3.D2, R3.Pin_1
  N16: Composant3.D4, JP5.4
  N17: Composant3.D5_PWM, JP5.3
  N18: Composant3.3V3, U3.S
  N19: JP3.4, U3.P
  N20: U1.P, U2.NC
  N21: U2.COIL2, Q1.C, D1.cathode
  N22: R2.Pin_0, D1.anode
  N23: Q1.B, R3.Pin_0

notes:
  3W, 5V = 0.6A
  1k Ohm
  enceinte  0.6A, arduino
  A0 - SDA - SCK - LED
  TFT Screen
  VCC - GND - CS - RESET
  GND - VCC - SW - DT
  CLK
  KY 040

custom parts:
  DFPlayer MINI: MP3 module by DFRobot.com for playing Music from an SD-Card. Supports WAV and MP3 files.
